# Fritzing sketch Control Box Wiring (saved by Fritzing 0.9.3b)

parts:
  5V_Regulator = Voltage Regulator - 5V [package="DPak [SMD]"]
  Adafruit_Logic_Level_Shifter = Adafruit 4-channel I2C-safe Bi-directional Logic Level Converter [part_number="Adafruit #757"]
  Adafruit_Metro_Mini = Adafruit Metro Mini [part_number="Adafruit #2590"]
  Adafruit_DotStar_Strip = LPD8806 RGB LED Strip
  PC_Power_12V = Power plug

nets:
  N1: 5V_Regulator.input_voltage, PC_Power_12V.VCC
  GND: 5V_Regulator.GND, Adafruit_Logic_Level_Shifter.GND, Adafruit_Metro_Mini.GND, Adafruit_DotStar_Strip.GND, PC_Power_12V.GND
  N2: 5V_Regulator.output_voltage, Adafruit_Logic_Level_Shifter.LV, Adafruit_DotStar_Strip.+5V
  N3: Adafruit_Logic_Level_Shifter.A3, Adafruit_DotStar_Strip.CI
  N4: Adafruit_Logic_Level_Shifter.A1, Adafruit_DotStar_Strip.DI
  N5: Adafruit_Logic_Level_Shifter.B3, Adafruit_Metro_Mini.IO13
  N6: Adafruit_Logic_Level_Shifter.B1, Adafruit_Metro_Mini.IO11

custom parts:
  Adafruit 4-channel I2C-safe Bi-directional Logic Level Converter: Because the Arduino (and Basic Stamp) are 5V devices, and most modern sensors, displays, flash cards and modes are 3.3V-only, many makers find that they need to perform level shifting/conversion to protect the 3.3V device from 5V. We do have some other handy level shifters in the shop, from the DIP 74LVC245 to the fancy bi-directional TXB0108. However, neither of these are happy to work with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
  Adafruit Metro Mini: We sure love the ATmega328 here at Adafruit, and we use them a lot for our own projects. The processor has plenty of GPIO, Analog inputs, hardware UART SPI and I2C, timers and PWM galore - just enough for most simple projects. When we need to go small, we use a Pro Trinket 3V or 5V, but if you want to have USB-to-Serial built in, we reach for an Adafruit METRO Mini. METRO Mini is the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
  LPD8806 RGB LED Strip: Digitally addressable RGB LED strip
